# Fritzing sketch Amplifier (saved by Fritzing 0.9.5d)
breadboards: 1

parts:
  Q3 = NPN-Transistor [package="TO92 [THT]"]
  C1 = Electrolytic Capacitor [capacitance=100µF package="100 mil [THT, electrolytic]"]
  R2 = Resistor [tolerance=±20% resistance=100 package=THT]
  R3 = Resistor [tolerance=±5% resistance=330 package=THT]
  C2 = Electrolytic Capacitor [capacitance=220µF package="100 mil [THT, electrolytic]"]
  R4 = Resistor [tolerance=±5% resistance=22 package=THT]
  C3 = Electrolytic Capacitor [capacitance=1µF package="100 mil [THT, electrolytic]"]
  R1 = Resistor [tolerance=±5% resistance=100k package="2512 [SMD]"]
  D1 = Rectifier Diode [part_number=1N4001 package="300 mil [THT]"]
  D2 = Rectifier Diode [part_number=1N4001 package="300 mil [THT]"]
  JP1 = Header 2 [package=molex-1x2_lock]
  JP2 = Header 2 [package=molex-1x2_lock]
  Q2 = PNP-Transistor [package="TO92 [THT]"]
  Q1 = NPN-Transistor [package="TO92 [THT]"]

nets:
  GND: Q3.E, C2.-, JP2.2, Q2.C
  N1: Q3.B, C3.+, R1.Pin_0
  N2: Q3.C, D2.cathode, Q2.B
  N3: C1.-, R1.Pin_1
  N4: C1.+, R2.Pin_1, R3.Pin_1, JP1.2
  N5: R2.Pin_0, C2.+, R4.Pin_0, JP1.1, Q1.C
  N6: R3.Pin_0, D1.anode, Q1.B
  5V: R4.Pin_1
  N7: C3.-, JP2.1
  N8: D1.cathode, D2.anode
  N9: Q2.E, Q1.E
